# Fritzing sketch Led + switch (saved by Fritzing 0.9.3b)

parts:
  LED1 = LED - 5mm [color="Green (565nm)" package="5 mm [THT]"]
  Power_plug1 = Power plug
  R1 = Resistor [tolerance=±5% resistance=1.5k package=THT]  # not connected
  U1 = SWITCH-SPST-2 [package=switch-spst-vertical]
  M1 = DC Motor

nets:
  N1: LED1.cathode, Power_plug1.GND, M1.pin_2
  N2: Power_plug1.VCC, U1.O
  N3: U1.P, M1.pin_1

notes:
  1,5K
  Switch
  24V
