# Fritzing sketch Wiring-sketch (saved by Fritzing 0.9.3b)
perfboards: 1

parts:
  Part1 = Adafruit TCA9548A
  A1 = AS5600 module
  A2 = AS5600 module
  A3 = IR Infrared Slotted Optical Speed Measuring Sensor
  A4 = IR Infrared Slotted Optical Speed Measuring Sensor
  A5 = IR Infrared Slotted Optical Speed Measuring Sensor
  A6 = IR Infrared Slotted Optical Speed Measuring Sensor
  A7 = BTS960
  A8 = BTS960
  J6 = male pin header, 6 pins [form="♂ (male)"]
  J7 = male pin header, 3 pins [form="♂ (male)"]
  J8 = male pin header, 3 pins [form="♂ (male)"]
  J9 = male pin header, 2 pins [form="♂ (male)"]
  J10 = male pin header, 2 pins [form="♂ (male)"]
  U1 = Gagagu Main PCB [chip_label=IC package="SIP (Single Inline) [THT]"]

nets:
  N1: Part1.VCC, U1.pin21
  N2: Part1.GND, U1.pin20
  N3: Part1.INPUTSDA, U1.pin22
  N4: Part1.INPUTSCL, Part1.RESET, U1.pin23
  N5: Part1.0SDA, A1.Pin_5, J6.pin6, J10.pin1
  N6: Part1.0SCL, Part1.1SDA, A1.Pin_6, A2.Pin_5, J6.pin5, J10.pin2
  N7: Part1.1SCL, A2.Pin_6
  N8: A1.Pin_1, J6.pin2, J7.pin2, J8.pin2, J9.pin1, U1.pin9
  N9: A1.Pin_3, J6.pin1, J7.pin3, J8.pin3, J9.pin2, U1.pin8
  N10: A2.Pin_1, U1.pin25
  N11: A2.Pin_3, U1.pin24
  N12: A3.Pin_1, J6.pin4, J8.pin1, U1.pin10
  N13: A4.Pin_1, J6.pin3, J7.pin1, U1.pin13
  N14: A5.Pin_1, U1.pin16
  N15: A5.Pin_2, U1.pin15
  N16: A5.Pin_3, U1.pin14
  N17: A6.Pin_1, U1.pin19
  N18: A6.Pin_2, U1.pin18
  N19: A6.Pin_3, U1.pin17
  N20: A7.Pin_1, U1.pin34
  N21: A7.Pin_3, U1.pin37
  N22: A7.Pin_4, U1.pin39
  N23: A7.Pin_5, U1.pin35
  N24: A7.Pin_7, U1.pin36
  N25: A7.Pin_8, U1.pin38
  N26: A8.Pin_1, U1.pin28
  N27: A8.Pin_3, U1.pin31
  N28: A8.Pin_4, U1.pin33
  N29: A8.Pin_5, U1.pin29
  N30: A8.Pin_7, U1.pin30
  N31: A8.Pin_8, U1.pin32
  N32: U1.pin26, U1.pin43
  N33: U1.pin27, U1.pin44
  N34: U1.pin40, U1.pin45
  N35: U1.pin41, U1.pin46
  N36: U1.pin42, U1.pin47

notes:
  The VCC and GND wires for the endstop sensors are not connected here for brevity. Use a 3-wire connector. See wiki for more.
  Left & Right Endstop sensors
  Up & Down Endstop sensors
  Roll Encoder
  Roll Motor Driver
  Pitch Encoder
  Pitch Motor Driver
  Main PCB
  TCA9548 I2C Mux
  Frame patch panel

custom parts:
  Adafruit TCA9548A: You just found the perfect I2C sensor, and you want to wire up two or three or more of them to your Arduino when you realize "Uh oh, this chip has a fixed I2C address, and from what I know about I2C, you cannot have two devices with the same address on the same SDA/SCL pins!" Are you out of luck? You would be, if you didn't have this ultra-cool TCA9548A 1-to-8 I2C multiplexer! Finally, a way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
  AS5600 module: .This module is mainly placed behind the stepper motor to obtain the rotation angle of the stepper motor.
  IR Infrared Slotted Optical Speed Measuring Sensor: IR Infrared Slotted Optical Speed Measuring Sensor Detection Optocoupler Module.
  BTS960: .The BTS7960 is a fully integrated high current H bridge module for motor drive applications.
  Gagagu Main PCB: Arduino FFB Yoke 2.0
