# Fritzing sketch Yoke controller (saved by Fritzing 0.9.3b)

parts:
  U3 = Gagagu Yoke PCB 2.0 [chip_label=IC package="SIP (Single Inline) [THT]"]
  S3 = JOYSTICK_MINI [package=joystick_mini]
  U4 = Gagagu Main PCB [chip_label=IC package="SIP (Single Inline) [THT]"]
  S4 = Round Pushbutton
  S7 = Round Pushbutton

nets:
  N1: U3.pin1, U4.pin1
  N2: U3.pin2, U4.pin2
  N3: U3.pin3, U4.pin3
  N4: U3.pin4, U4.pin4
  N5: U3.pin5, U4.pin5
  N6: U3.pin10, S4.leg1
  N7: U3.pin11, S7.leg1
  N8: U3.pin17, S4.leg0, S7.leg0
  N9: U3.pin18, S3.RIGHT
  N10: U3.pin19, S3.LEFT
  N11: U3.pin20, S3.DOWN
  N12: U3.pin21, S3.UP
  N13: U3.pin22, S3.CENT
  N14: U3.pin26, S3.GND

notes:
  This component image of the hat switch is mirrored from reality, i.e wrong. Look at the actual picture
  in the wiki for reference.
  Wire up all buttons and switches with one connection to a B-input and the other through a shared common (GND).
  Yoke Controller wiring

custom parts:
  Gagagu Yoke PCB 2.0: Arduino FFB Yoke Board 2.0
  Gagagu Main PCB: Arduino FFB Yoke 2.0
